// Logisim project S257-01.circ as structural Verilog: 8 circuits, main circuit main
module main (
  input  RST,
  input  PWR,
  input  CLK,
  input  [7:0] in_4
);

  wire and_2_out, and_3_out, and_4_out, and_5_out, and_6_out, buffer32_1_out_2, buffer32_2_out_2,
       buffer32_3_out_2, buffer_1_out, buffer_2_out, buffer_3_out, buffer_4_out, buffer_5_out, buffer_6_out,
       buffer_7_out, buffer_8_out, buffer_9_out, buffer_10_out, buffer_11_out, buffer_12_out, CLK_t,
       clock_1_out, CU_RST, decoder_2_out1, decoder_2_out2, decoder_2_out3, decoder_2_out4, EA, EB, EC, ED,
       EE, EF, nor_1_out, not_1_out, not_2_out, not_3_out, not_4_out, not_5_out, not_6_out, or_2_out,
       or_4_out, or_6_out, or_7_out, or_8_out, or_9_out, pulse4_1_out_2, PWR_t, RST_t, t_ff_1_q, t_ff_1_qn;
  wire [2:0] counter_3_q;
  wire [3:0] CTRL, demultiplexer_1_out2, demultiplexer_3_out0, FLAG, FLG, MEM;
  wire [7:0] A, B, C, controlled_buffer_2_out, D, demultiplexer_1_out0, demultiplexer_1_out1,
       demultiplexer_2_out0, demultiplexer_2_out1, demultiplexer_3_out1, E, F, M1, M2, M3, M4,
       multiplexer_1_out, multiplexer_2_out, multiplexer_3_out, multiplexer_5_out, or_3_out, or_5_out, R,
       register_11_q, WA, xor_1_out;
  wire [7:4] demultiplexer_1_out2_2, demultiplexer_3_out0_2;
  wire [15:0] counter_1_q, counter_2_q, multiplexer_4_out;

  or or_1 (RST_t, RST, and_2_out, CU_RST);
  Clock clock_1 (.out(clock_1_out));
  T_Flip_Flop t_ff_1 (.clk(or_2_out), .T(or_2_out), .Q(t_ff_1_q), .Qn(t_ff_1_qn));  // open: preset, reset
  or or_2 (or_2_out, PWR_t, PWR);
  not not_1 (not_1_out, t_ff_1_qn);
  Demultiplexer #(.select(2), .width(8), .enable("false")) demultiplexer_1 (
    .out0(demultiplexer_1_out0), .out1(demultiplexer_1_out1),
    .out2({demultiplexer_1_out2_2, demultiplexer_1_out2}), .in(M2), .sel(CTRL[3:2]));  // open: out3
  Register #(.trigger("falling")) register_1 (.D(WA), .en(EA), .Q(A), .clk(CLK_t), .clr(RST_t));
  Register #(.trigger("falling")) register_2 (.D(WA), .en(EB), .Q(B), .clk(CLK_t), .clr(RST_t));
  Register #(.trigger("falling")) register_3 (.D(WA), .en(EC), .Q(C), .clk(CLK_t), .clr(RST_t));
  Register #(.trigger("falling")) register_4 (.D(WA), .en(ED), .Q(D), .clk(CLK_t), .clr(RST_t));
  Register #(.trigger("falling")) register_5 (.D(WA), .en(EE), .Q(E), .clk(CLK_t), .clr(RST_t));
  and and_1 (CLK_t, clock_1_out, t_ff_1_q);
  and and_2 (and_2_out, not_1_out, t_ff_1_qn);
  Decoder #(.select(4), .enable("false")) decoder_1 (
    .out1(EA), .out2(EB), .out3(EC), .out4(ED), .out5(EE), .out6(EF), .sel(demultiplexer_1_out0[3:0]));  // open: out0, out7, out8, out9, out10, out11, out12, out13, out14, out15
  Multiplexer #(.select(4), .width(8), .enable("false")) multiplexer_1 (
    .in0({8{1'b0}}), .in1(A), .in2(B), .in3(C), .in4(D), .in5(E), .in6(F), .in7(R), .out(multiplexer_1_out),
    .sel(demultiplexer_1_out2));  // open: in8, in9, in10, in11, in12, in13, in14, in15
  and and_3 (and_3_out, CTRL[2], CTRL[3]);
  Random random_1 (.clr(and_4_out), .clk(CLK_t), .out(R));  // open: next
  not not_2 (not_2_out, RST_t);
  and and_4 (and_4_out, not_2_out, RST_t);
  assign or_3_out = demultiplexer_1_out1 | multiplexer_1_out;  // OR_Gate or_3, 8 bits wide
  assign xor_1_out = or_3_out ^ F;  // XOR_Gate xor_1, 8 bits wide
  Register #(.trigger("high")) register_6 (.D(multiplexer_2_out), .en(or_4_out), .Q(F), .clk(CLK_t), .clr(RST_t));
  Multiplexer #(.width(8), .enable("false")) multiplexer_2 (
    .in0(WA), .in1({F[7:4], FLG}), .out(multiplexer_2_out), .sel(and_3_out));
  or or_4 (or_4_out, and_3_out, EF);
  Demultiplexer #(.width(8), .enable("false")) demultiplexer_2 (
    .out0(demultiplexer_2_out0), .out1(demultiplexer_2_out1), .in(M3), .sel(CTRL[0]));
  nor nor_1 (nor_1_out, xor_1_out[3], xor_1_out[0], xor_1_out[1], xor_1_out[2], xor_1_out[4], xor_1_out[5], xor_1_out[6], xor_1_out[7]);
  Multiplexer #(.select(4), .width(8), .enable("false")) multiplexer_3 (
    .in0(demultiplexer_2_out1), .in1(A), .in2(B), .in3(C), .in4(D), .in5(E), .in6(F), .in7(R),
    .out(multiplexer_3_out), .sel(demultiplexer_2_out0[3:0]));  // open: in8, in9, in10, in11, in12, in13, in14, in15
  assign or_5_out = demultiplexer_1_out1 | in_4 | multiplexer_1_out;  // OR_Gate or_5, 8 bits wide
  and and_5 (and_5_out, nor_1_out, MEM[0]);
  buffer32 buffer32_1 (.in_1(buffer32_2_out_2), .out_2(buffer32_1_out_2));
  buffer32 buffer32_2 (.in_1(MEM[1]), .out_2(buffer32_2_out_2));
  buf buffer_1 (buffer_1_out, buffer32_1_out_2);
  and and_6 (and_6_out, buffer32_2_out_2, ~buffer32_1_out_2);  // AND_Gate
  alu alu_1 (.A(multiplexer_3_out), .B(multiplexer_5_out), .S(WA), .OP(FLAG), .FLAG(FLG));
  or or_6 (or_6_out, and_5_out, buffer32_2_out_2);
  or or_7 (or_7_out, buffer_3_out, and_6_out, pulse4_1_out_2, and_5_out);
  Multiplexer #(.width(16), .enable("false")) multiplexer_4 (
    .in0({multiplexer_3_out, multiplexer_5_out}), .in1(counter_2_q), .out(multiplexer_4_out),
    .sel(buffer32_1_out_2));
  buf buffer_2 (buffer_2_out, buffer_4_out);
  buf buffer_3 (buffer_3_out, buffer_2_out);
  buf buffer_4 (buffer_4_out, buffer_1_out);
  pulse4 pulse4_1 (.in_1(CLK_t), .out_2(pulse4_1_out_2));
  buf buffer_5 (buffer_5_out, pulse4_1_out_2);
  buf buffer_6 (buffer_6_out, buffer_5_out);
  buf buffer_7 (buffer_7_out, buffer_6_out);
  buf buffer_8 (buffer_8_out, buffer_9_out);
  or or_8 (or_8_out, buffer_8_out, buffer32_3_out_2);
  buf buffer_9 (buffer_9_out, buffer_7_out);
  buffer32 buffer32_3 (.in_1(CLK_t), .out_2(buffer32_3_out_2));
  assign WA = MEM[2] ? register_11_q : 8'bz;  // Controlled_Buffer controlled_buffer_1
  buf buffer_10 (buffer_10_out, MEM[3]);
  Counter #(.width(16), .max('hffff)) counter_1 (
    .load(or_6_out), .D(multiplexer_4_out), .Q(counter_1_q), .clk(or_7_out), .clr(RST_t));  // open: count, carry
  buf buffer_11 (buffer_11_out, MEM[3]);
  Counter #(.width(16), .max('hffff)) counter_2 (
    .load(MEM[1]), .D(counter_1_q), .Q(counter_2_q), .clk(MEM[1]), .clr(not_3_out));  // open: count, carry
  not not_3 (not_3_out, CLK_t);
  Decoder #(.select(3), .enable("false")) decoder_2 (
    .out1(decoder_2_out1), .out2(decoder_2_out2), .out3(decoder_2_out3), .out4(decoder_2_out4),
    .sel(counter_3_q));  // open: out0, out5, out6, out7
  Counter #(.width(3), .max('h7)) counter_3 (
    .Q(counter_3_q), .clk(or_8_out), .clr(not_4_out));  // open: load, D, count, carry
  not not_4 (not_4_out, CLK_t);
  Multiplexer #(.select(4), .width(8), .enable("false")) multiplexer_5 (
    .in0(demultiplexer_3_out1), .in1(A), .in2(B), .in3(C), .in4(D), .in5(E), .in6(F), .in7(R),
    .out(multiplexer_5_out), .sel(demultiplexer_3_out0));  // open: in8, in9, in10, in11, in12, in13, in14, in15
  assign controlled_buffer_2_out = buffer_12_out ? or_5_out : 8'bz;  // Controlled_Buffer controlled_buffer_2
  RAM #(.addrWidth(16), .trigger("high"), .\type ("nonvolatile"), .databus("bidir")) ram_1 (
    .addr(counter_1_q), .data(controlled_buffer_2_out));  // open: we, oe, clk
  buf buffer_12 (buffer_12_out, buffer_10_out);
  not not_5 (not_5_out, MEM[3]);
  // Buffer buffer_13 has open pins: in=buffer_11_out, out=open
  Demultiplexer #(.width(8), .enable("false")) demultiplexer_3 (
    .out0({demultiplexer_3_out0_2, demultiplexer_3_out0}), .out1(demultiplexer_3_out1), .in(M4), .sel(CTRL[1]));
  cu cu_1 (.OP(M1), .ALU(FLAG), .CTRL(CTRL), .PWR(PWR_t), .RST(CU_RST), .MEM(MEM), .in_1(RST_t));
  Register register_7 (.D(controlled_buffer_2_out), .Q(M1), .clk(decoder_2_out1), .clr(or_9_out));  // open: en
  Register register_8 (.D(controlled_buffer_2_out), .Q(M2), .clk(decoder_2_out2), .clr(or_9_out));  // open: en
  Register register_9 (.D(controlled_buffer_2_out), .Q(M3), .clk(decoder_2_out3), .clr(or_9_out));  // open: en
  // Probe on controlled_buffer_2_out
  Register register_10 (.D(controlled_buffer_2_out), .Q(M4), .clk(decoder_2_out4), .clr(or_9_out));  // open: en
  not not_6 (not_6_out, CLK_t);
  or or_9 (or_9_out, not_6_out, RST_t);
  Register register_11 (.D(controlled_buffer_2_out), .Q(register_11_q), .clk(MEM[2]), .clr(RST_t));  // open: en

  // Other names for the same wires on the sheet: WB[7:0] = WA; WC[7:0] = WA; WD[7:0] = WA; WE[7:0] = WA; WF[7:0] = WA

  // Notes on the sheet:
  //   contents of ram_1 (hex, n*v repeats v):
  //   4 4 4 0 4 1 aa 0 4 2 bb 0 3 1 2 0 7 0 1 bb 53 4 0 24 53 6 0 1c 4 5 3 0 53 6 0 1c 4 1 11 0 4 2 22 0
  //   10 3 1 2 7 0 3 33 53 4 0 44 53 6 0 3c 4 5 10 0 53 6 0 3c 4 1 11 0 4 2 22 0 11 3 1 2 7 0 3 34 53 4 0
  //   64 53 6 0 5c 4 5 11 0 53 6 0 5c 4 1 11 0 4 2 22 0 12 3 2 1 7 0 3 11 53 4 0 84 53 6 0 7c 4 5 12 0 53
  //   6 0 7c 4 1 11 0 4 2 22 0 12 3 2 1 7 0 3 10 53 4 0 a4 53 6 0 9c 4 5 13 0 53 6 0 9c 4 1 4 0 4 2 22 0
  //   14 3 2 1 7 0 3 88 53 4 0 c4 53 6 0 bc 4 5 14 0 53 6 0 bc 4 1 11 0 4 2 22 0 15 3 2 1 7 0 3 2 53 4 0
  //   e4 53 6 0 dc 4 5 15 0 53 6 0 dc 4 1 11 0 4 2 24 0 16 3 2 1 7 0 3 2 53 4 1 5 53 6 0 fc 4 5 16 0 53 6
  //   0 fc 4 1 11 0 4 2 23 0 17 3 2 1 7 0 3 1 53 4 1 25 53 6 1 1d 4 5 17 0 53 6 1 1d 4 1 12 0 4 2 20 0 18
  //   3 2 1 7 0 3 22 53 4 1 45 53 6 1 3d 4 5 18 0 53 6 1 3d 4 1 11 0 4 2 23 0 19 3 2 1 7 0 3 22 53 4 1 65
  //   53 6 1 5d 4 5 19 0 53 6 1 5d 2
endmodule

module cu (
  input  in_1,
  input  [7:0] OP,
  output [3:0] ALU,
  output [3:0] CTRL,
  output [3:0] MEM,
  output PWR,
  output RST
);

  wire buffer16_1_out_2, buffer16_2_out_2, buffer32_1_out_2, buffer32_4_out_2, buffer32_5_out_2,
       buffer32_6_out_2, buffer32_7_out_2, buffer_2_out, buffer_3_out, buffer_4_out, nor_1_out, xor_1_out;
  wire [11:4] pla_1_out;

  PLA #(.in_width(8), .out_width(14), .\table ("00000000 00000000001111 # NOP\n00000001 10000000000000 # RST\n00000010 01000000000000 # OFF\n00000100 00000000010000 # MOV_V\n00000101 00000011000001 # CMP_RR\n00000110 00000011010001 # CMP_VR\n00000111 00000011100001 # CMP_RV\n00001000 00000011110001 # CMP_VV\n00010000 00000000000000 # ADD_RR\n00010001 00000000001000 # ADC_RR\n00010010 00000000000001 # SUB_RR\n00010011 00000000001001 # SBB_RR\n00010100 00000000000010 # MUL_RR\n00010101 00000000000011 # DIV_RR\n00010110 00000000000100 # MOD_RR\n00010111 00000000000101 # AND_RR\n00011000 00000000000110 # OR_RR\n00011001 00000000000111 # XOR_RR\n00100000 00000000010000 # ADD_VR\n00100001 00000000011000 # ADC_VR\n00100010 00000000010001 # SUB_VR\n00100011 00000000011001 # SBB_VR\n00100100 00000000010010 # MUL_VR\n00100101 00000000010011 # DIV_VR\n00100110 00000000010100 # MOD_VR\n00100111 00000000010101 # AND_VR\n00101000 00000000010110 # OR_VR\n00101001 00000000010111 # XOR_VR\n00110000 00000000100000 # ADD_RV\n00110001 00000000101000 # ADC_RV\n00110010 00000000100001 # SUB_RV\n00110011 00000000101001 # SBB_RV\n00110100 00000000100010 # MUL_RV\n00110101 00000000100011 # DIV_RV\n00110110 00000000100100 # MOD_RV\n00110111 00000000100101 # AND_RV\n00111000 00000000100110 # OR_RV\n00111001 00000000100111 # XOR_RV\n01000000 00000000110000 # ADD_VV\n01000001 00000000111000 # ADC_VV\n01000010 00000000110001 # SUB_VV\n01000011 00000000111001 # SBB_VV\n01000100 00000000110010 # MUL_VV\n01000101 00000000110011 # DIV_VV\n01000110 00000000110100 # MOD_VV\n01000111 00000000110101 # AND_VV\n01001000 00000000110110 # OR_VV\n01001001 00000000110111 # XOR_VV\n01010000 00000110001111 # JMP_RRR\n01010001 00000110011111 # JMP_RVR\n01010010 00000110101111 # JMP_RRV\n01010011 00000110111111 # JMP_RVV\n01010100 00000101001111 # JMP_VRR\n01010101 00000101011111 # JMP_VVR\n01010110 00000101101111 # JMP_VRV\n01010111 00000101111111 # JMP_VVV\n01100000 00011010001111 # GET_RR\n01100001 00011010101111 # GET_VR\n01100010 00011010011111 # GET_RV\n01100011 00011010111111 # GET_VV\n01100100 00101010001111 # SET_RRR\n01100101 00101010101111 # SET_RVR\n01100110 00101010011111 # SET_RRV\n01100111 00101010111111 # SET_RVV\n01101000 00101001001111 # SET_VRR\n01101001 00101001101111 # SET_VVR\n01101010 00101001011111 # SET_VRV\n01101011 00101001111111 # SET_VVV")) pla_1 (
    .in(OP), .out({RST, PWR, pla_1_out, ALU}));
  Pull_Resistor pull_resistor_1 (.node(CTRL));
  assign CTRL = buffer32_1_out_2 ? pla_1_out[7:4] : 4'bz;  // Controlled_Buffer controlled_buffer_1
  buffer32 buffer32_1 (.in_1(xor_1_out), .out_2(buffer32_1_out_2));
  xor xor_1 (xor_1_out, in_1, nor_1_out);
  nor nor_1 (nor_1_out, buffer_4_out, MEM[2]);
  buffer32 buffer32_2 (.in_1(pla_1_out[8]), .out_2(MEM[0]));
  buffer32 buffer32_3 (.in_1(pla_1_out[9]), .out_2(MEM[1]));
  buffer32 buffer32_4 (.in_1(buffer32_5_out_2), .out_2(buffer32_4_out_2));
  buffer16 buffer16_1 (.out_2(buffer16_1_out_2), .in_1(buffer32_4_out_2));
  buffer32 buffer32_5 (.in_1(pla_1_out[10]), .out_2(buffer32_5_out_2));
  buffer16 buffer16_2 (.out_2(buffer16_2_out_2), .in_1(buffer32_6_out_2));
  buffer32 buffer32_6 (.in_1(buffer32_7_out_2), .out_2(buffer32_6_out_2));
  buffer32 buffer32_7 (.in_1(pla_1_out[11]), .out_2(buffer32_7_out_2));
  buf buffer_1 (MEM[2], buffer_2_out);
  buf buffer_2 (buffer_2_out, buffer16_1_out_2);
  buf buffer_3 (buffer_3_out, buffer16_2_out_2);
  buf buffer_4 (buffer_4_out, buffer_3_out);
  Pull_Resistor pull_resistor_2 (.node(MEM[3]));
  assign MEM[3] = buffer32_1_out_2 ? buffer_4_out : 1'bz;  // Controlled_Buffer controlled_buffer_2
endmodule

module alu (
  input  [3:0] OP,
  input  [7:0] A,
  input  [7:0] B,
  output [7:0] S,
  output [3:0] FLAG
);

  wire adder_1_cout, comparator_1_eq, nand_1_out, not_1_out, subtractor_1_bout;
  wire [3:0] multiplexer_1_out;
  wire [7:0] adder_1_out, and_1_out, divider_1_out, divider_1_rem, multiplexer_2_out, multiplier_1_cout,
       multiplier_1_out, or_1_out, register_1_q, subtractor_1_out, xor_1_out;

  assign and_1_out = A & B;  // AND_Gate and_1, 8 bits wide
  assign or_1_out = A | B;  // OR_Gate or_1, 8 bits wide
  Adder adder_1 (.a(A), .b(B), .out(adder_1_out), .cin(OP[3]), .cout(adder_1_cout));
  Subtractor subtractor_1 (.a(A), .b(B), .out(subtractor_1_out), .bin(OP[3]), .bout(subtractor_1_bout));
  Multiplier multiplier_1 (.a(A), .b(B), .out(multiplier_1_out), .cout(multiplier_1_cout));  // open: cin
  Comparator comparator_1 (.a(multiplier_1_cout), .b({8{1'b0}}), .eq(comparator_1_eq));  // open: gt, lt
  Divider divider_1 (.a(A), .b(B), .out(divider_1_out), .rem(divider_1_rem));  // open: upper
  assign xor_1_out = A ^ B;  // XOR_Gate xor_1, 8 bits wide
  Comparator comparator_2 (
    .a(A), .b(B), .gt(multiplexer_1_out[1]), .eq(multiplexer_1_out[2]), .lt(multiplexer_1_out[3]));
  Multiplexer #(.select(2), .enable("false")) multiplexer_1 (
    .in0(adder_1_cout), .in1(subtractor_1_bout), .in2(not_1_out), .in3(1'b0), .out(multiplexer_1_out[0]),
    .sel(OP[1:0]));
  not not_1 (not_1_out, comparator_1_eq);
  Register #(.trigger("high")) register_1 (.D(multiplexer_2_out), .Q(register_1_q), .clk(1'b1));  // open: en, clr
  Multiplexer #(.select(3), .width(8), .enable("false")) multiplexer_2 (
    .in0(adder_1_out), .in1(subtractor_1_out), .in2(multiplier_1_out), .in3(divider_1_out),
    .in4(divider_1_rem), .in5(and_1_out), .in6(or_1_out), .in7(xor_1_out), .out(multiplexer_2_out),
    .sel(OP[2:0]));
  Register #(.width(4), .trigger("high")) register_2 (.D(multiplexer_1_out), .Q(FLAG), .clk(1'b1));  // open: en, clr
  nand nand_1 (nand_1_out, OP[0], OP[1], OP[2], OP[3]);
  assign S = nand_1_out ? register_1_q : 8'bz;  // Controlled_Buffer controlled_buffer_1
endmodule

module alu1bit (
  input  A,
  input  B,
  input  Inv,
  input  [1:0] OP,
  input  Cin,
  output S,
  output Cout
);

  wire and_1_out, and_2_out, and_3_out, and_4_out, and_5_out, and_6_out, decoder_1_out0, decoder_1_out1,
       decoder_1_out2, decoder_1_out3, or_1_out, or_3_out, or_5_out, xor_1_out, xor_2_out, xor_3_out;

  xor xor_1 (xor_1_out, B, Inv);
  Decoder #(.select(2), .enable("false")) decoder_1 (
    .out0(decoder_1_out0), .out1(decoder_1_out1), .out2(decoder_1_out2), .out3(decoder_1_out3), .sel(OP));
  and and_1 (and_1_out, decoder_1_out3, xor_2_out);
  xor xor_2 (xor_2_out, A, xor_1_out);
  and and_2 (and_2_out, Cin, xor_2_out);
  and and_3 (and_3_out, A, xor_1_out);
  or or_1 (or_1_out, A, xor_1_out);
  and and_4 (and_4_out, or_1_out, decoder_1_out2);
  and and_5 (and_5_out, decoder_1_out0, xor_3_out);
  xor xor_3 (xor_3_out, xor_2_out, Cin);
  or or_2 (Cout, and_2_out, and_3_out);
  and and_6 (and_6_out, and_3_out, decoder_1_out1);
  or or_3 (or_3_out, and_4_out, and_1_out);
  or or_4 (S, or_3_out, or_5_out);
  or or_5 (or_5_out, and_5_out, and_6_out);
endmodule

module pulse4 (
  input  in_1,
  output out_2
);

  wire and_1_out, and_2_out, and_3_out, and_4_out, buffer_1_out, buffer_2_out, buffer_3_out, buffer_4_out,
       buffer_5_out, buffer_6_out, buffer_7_out, buffer_8_out, buffer_9_out, buffer_10_out, buffer_11_out,
       buffer_12_out, buffer_13_out, buffer_14_out, buffer_15_out, buffer_16_out, buffer_17_out,
       buffer_18_out, buffer_19_out, buffer_20_out, buffer_21_out, buffer_22_out, buffer_23_out,
       buffer_24_out, not_1_out, not_2_out, not_3_out, not_4_out;

  buf buffer_1 (buffer_1_out, in_1);
  buf buffer_2 (buffer_2_out, in_1);
  buf buffer_3 (buffer_3_out, in_1);
  buf buffer_4 (buffer_4_out, buffer_3_out);
  buf buffer_5 (buffer_5_out, buffer_4_out);
  buf buffer_6 (buffer_6_out, in_1);
  buf buffer_7 (buffer_7_out, buffer_8_out);
  buf buffer_8 (buffer_8_out, in_1);
  buf buffer_9 (buffer_9_out, buffer_10_out);
  buf buffer_10 (buffer_10_out, buffer_11_out);
  buf buffer_11 (buffer_11_out, in_1);
  buf buffer_12 (buffer_12_out, buffer_13_out);
  buf buffer_13 (buffer_13_out, buffer_1_out);
  buf buffer_14 (buffer_14_out, buffer_12_out);
  buf buffer_15 (buffer_15_out, buffer_2_out);
  buf buffer_16 (buffer_16_out, buffer_15_out);
  buf buffer_17 (buffer_17_out, buffer_18_out);
  buf buffer_18 (buffer_18_out, buffer_16_out);
  buf buffer_19 (buffer_19_out, buffer_21_out);
  buf buffer_20 (buffer_20_out, buffer_19_out);
  buf buffer_21 (buffer_21_out, buffer_5_out);
  and and_1 (and_1_out, in_1, not_1_out);
  not not_1 (not_1_out, in_1);
  buf buffer_22 (buffer_22_out, buffer_6_out);
  and and_2 (and_2_out, buffer_22_out, not_2_out);
  not not_2 (not_2_out, buffer_7_out);
  buf buffer_23 (buffer_23_out, buffer_9_out);
  and and_3 (and_3_out, buffer_23_out, not_3_out);
  not not_3 (not_3_out, buffer_14_out);
  buf buffer_24 (buffer_24_out, buffer_17_out);
  and and_4 (and_4_out, buffer_24_out, not_4_out);
  not not_4 (not_4_out, buffer_20_out);
  or or_1 (out_2, and_1_out, and_2_out, and_3_out, and_4_out);
endmodule

module buffer32 (
  input  in_1,
  output out_2
);

  wire and_1_out, not_1_out, not_2_out;

  and and_1 (and_1_out, in_1, ~out_2, not_1_out);  // AND_Gate
  not not_1 (not_1_out, and_1_out);
  Counter #(.width(3), .max('h7), .ongoal("stay")) counter_1 (
    .carry(out_2), .clk(and_1_out), .clr(not_2_out));  // open: load, D, count, Q
  not not_2 (not_2_out, in_1);
endmodule

module buffer16 (
  input  in_1,
  output out_2
);

  wire and_1_out, not_1_out, not_2_out;

  and and_1 (and_1_out, in_1, ~out_2, not_1_out);  // AND_Gate
  not not_1 (not_1_out, and_1_out);
  Counter #(.width(2), .max('h3), .ongoal("stay")) counter_1 (
    .carry(out_2), .clk(and_1_out), .clr(not_2_out));  // open: load, D, count, Q
  not not_2 (not_2_out, in_1);
endmodule

module test (
  input  [7:0] in_1,
  input  in_2,
  input  [15:0] in_3,
  input  in_4,
  input  in_5,
  input  in_6,
  output [7:0] out_7
);

  RAM #(.addrWidth(16), .trigger("high"), .databus("bidir")) ram_1 (.addr(in_3), .data(out_7));  // open: we, oe, clk
  assign out_7 = in_2 ? in_1 : 8'bz;  // Controlled_Buffer controlled_buffer_1
endmodule
