// Logisim project Saphyr-1.circ as structural Verilog
module main (
  input  PWR,
  output GND
);

  wire and_1_out, and_2_out, and_3_out, and_4_out, and_5_out, and_6_out, and_7_out, and_8_out, and_9_out,
       and_10_out, and_11_out, and_12_out, and_13_out, and_14_out, and_15_out, and_16_out, and_17_out, CLK,
       clock_1_out, D0, D1, D2, D3, D4, D5, D6, D7, ext_1_d0_2, ext_1_d1_2, ext_1_d2_2, ext_1_d3_2,
       ext_1_d4_2, ext_1_d5_2, ext_1_d6_2, ext_1_d7_2, ext_1_gnd_2, not_1_out, not_2_out, not_3_out,
       not_4_out, not_5_out, not_6_out, not_7_out, not_8_out, or_1_out, ram_1k_1_gnd, ram_8k_1_gnd,
       ram_16k_1_gnd, rom_2k_1_gnd, rom_4k_1_gnd, RST, RW, s257_01_1_a0, s257_01_1_a1, s257_01_1_a2,
       s257_01_1_a3, s257_01_1_a4, s257_01_1_a5, s257_01_1_a6, s257_01_1_a7, s257_01_1_a8, s257_01_1_a9,
       s257_01_1_a10, s257_01_1_a11, s257_01_1_a12, s257_01_1_a13, s257_01_1_a14, s257_01_1_a15,
       s257_01_1_stp, states_1_e_vpu, t_ff_1_q, vpu_1_vram;

  S257_01 s257_01_1 (
    .A0(s257_01_1_a0), .A1(s257_01_1_a1), .A2(s257_01_1_a2), .A3(s257_01_1_a3), .A4(s257_01_1_a4),
    .A5(s257_01_1_a5), .A6(s257_01_1_a6), .A7(s257_01_1_a7), .A8(s257_01_1_a8), .A9(s257_01_1_a9),
    .A10(s257_01_1_a10), .A11(s257_01_1_a11), .A12(s257_01_1_a12), .A13(s257_01_1_a13), .A14(s257_01_1_a14),
    .A15(s257_01_1_a15), .D0_2(D0), .D1_2(D1), .D2_2(D2), .D3_2(D3), .D4_2(D4), .D5_2(D5), .D6_2(D6),
    .D7_2(D7), .STP(s257_01_1_stp), .RST(RST), .GND(GND), .R_W(RW), .CLK_2(CLK), .D0(D0), .D1(D1), .D2(D2),
    .D3(D3), .D4(D4), .D5(D5), .D6(D6), .D7(D7), .CLK(clock_1_out), .PWR(t_ff_1_q));
  ext ext_1 (
    .D_CPU_0_2(D0), .D_CPU_1_2(D1), .D_CPU_2_2(D2), .D_CPU_3_2(D3), .D_CPU_4_2(D4), .D_CPU_5_2(D5),
    .D_CPU_6_2(D6), .D_CPU_7_2(D7), .D3_2(ext_1_d3_2), .D4_2(ext_1_d4_2), .D5_2(ext_1_d5_2),
    .D6_2(ext_1_d6_2), .D7_2(ext_1_d7_2), .D0_2(ext_1_d0_2), .D1_2(ext_1_d1_2), .D2_2(ext_1_d2_2),
    .GND_2(ext_1_gnd_2), .R_W(RW), .ENA(and_2_out), .D_CPU_3(D3), .D_CPU_4(D4), .D_CPU_5(D5), .D_CPU_6(D6),
    .D_CPU_7(D7), .D_CPU_0(D0), .D_CPU_1(D1), .D_CPU_2(D2), .D0(ext_1_d0_2), .D1(ext_1_d1_2),
    .D2(ext_1_d2_2), .D3(ext_1_d3_2), .D4(ext_1_d4_2), .D5(ext_1_d5_2), .D6(ext_1_d6_2), .D7(ext_1_d7_2),
    .A_CPU_0(s257_01_1_a0), .A_CPU_1(s257_01_1_a1), .A_CPU_2(s257_01_1_a2), .A_CPU_3(s257_01_1_a3),
    .A_CPU_4(s257_01_1_a4), .A_CPU_5(s257_01_1_a5), .A_CPU_6(s257_01_1_a6), .A_CPU_7(s257_01_1_a7),
    .A_CPU_8(s257_01_1_a8), .A_CPU_9(s257_01_1_a9), .A_CPU_10(s257_01_1_a10), .A_CPU_11(s257_01_1_a11),
    .A_CPU_12(s257_01_1_a12), .A_CPU_13(s257_01_1_a13), .A_CPU_14(s257_01_1_a14), .PWR(t_ff_1_q), .CLK(CLK),
    .RST(RST));  // open: R_W_2, ENA_2, A0, A1, A2, A3, A4, A5, A6, A7, A8, A9, A10, A11, A12, A13, A14, PWR_2, CLK_2, RST_2, GND
  ram_16k ram_16k_1 (
    .GND(ram_16k_1_gnd), .D2_2(D2), .D3_2(D3), .D4_2(D4), .D5_2(D5), .D6_2(D6), .D7_2(D7), .D0_2(D0),
    .D1_2(D1), .A0(s257_01_1_a0), .A1(s257_01_1_a1), .A2(s257_01_1_a2), .A3(s257_01_1_a3), .A4(s257_01_1_a4),
    .A5(s257_01_1_a5), .A6(s257_01_1_a6), .A7(s257_01_1_a7), .A8(s257_01_1_a8), .A9(s257_01_1_a9),
    .A10(s257_01_1_a10), .A11(s257_01_1_a11), .A12(s257_01_1_a12), .A13(s257_01_1_a13), .PWR(t_ff_1_q),
    .CLK(CLK), .ENA(and_4_out), .R_W(RW), .RST(RST), .D0(D0), .D1(D1), .D2(D2), .D3(D3), .D4(D4), .D5(D5),
    .D6(D6), .D7(D7));
  ram_8k ram_8k_1 (
    .GND(ram_8k_1_gnd), .D2_2(D2), .D3_2(D3), .D4_2(D4), .D5_2(D5), .D6_2(D6), .D7_2(D7), .D0_2(D0),
    .D1_2(D1), .A0(s257_01_1_a0), .A1(s257_01_1_a1), .A2(s257_01_1_a2), .A3(s257_01_1_a3), .A4(s257_01_1_a4),
    .A5(s257_01_1_a5), .A6(s257_01_1_a6), .A7(s257_01_1_a7), .A8(s257_01_1_a8), .A9(s257_01_1_a9),
    .A10(s257_01_1_a10), .A11(s257_01_1_a11), .A12(s257_01_1_a12), .PWR(t_ff_1_q), .CLK(CLK),
    .ENA(and_6_out), .R_W(RW), .RST(RST), .D0(D0), .D1(D1), .D2(D2), .D3(D3), .D4(D4), .D5(D5), .D6(D6),
    .D7(D7));
  rom_4k rom_4k_1 (
    .GND(rom_4k_1_gnd), .D0(D0), .D1(D1), .D2(D2), .D3(D3), .D4(D4), .D5(D5), .D6(D6), .D7(D7), .R_W(RW),
    .CLK(CLK), .ENA(and_9_out), .PWR(t_ff_1_q), .A2(s257_01_1_a2), .A3(s257_01_1_a3), .A4(s257_01_1_a4),
    .A5(s257_01_1_a5), .A6(s257_01_1_a6), .A7(s257_01_1_a7), .A8(s257_01_1_a8), .A9(s257_01_1_a9),
    .A10(s257_01_1_a10), .A11(s257_01_1_a11), .A0(s257_01_1_a0), .A1(s257_01_1_a1));
  rom_2k rom_2k_1 (
    .GND(rom_2k_1_gnd), .D0(D0), .D1(D1), .D2(D2), .D3(D3), .D4(D4), .D5(D5), .D6(D6), .D7(D7), .R_W(RW),
    .CLK(CLK), .ENA(and_11_out), .PWR(t_ff_1_q), .A2(s257_01_1_a2), .A3(s257_01_1_a3), .A4(s257_01_1_a4),
    .A5(s257_01_1_a5), .A6(s257_01_1_a6), .A7(s257_01_1_a7), .A8(s257_01_1_a8), .A9(s257_01_1_a9),
    .A10(s257_01_1_a10), .A0(s257_01_1_a0), .A1(s257_01_1_a1));
  ram_1k ram_1k_1 (
    .GND(ram_1k_1_gnd), .D2_2(D2), .D3_2(D3), .D4_2(D4), .D5_2(D5), .D6_2(D6), .D7_2(D7), .D0_2(D0),
    .D1_2(D1), .A0(s257_01_1_a0), .A1(s257_01_1_a1), .A2(s257_01_1_a2), .A3(s257_01_1_a3), .A4(s257_01_1_a4),
    .A5(s257_01_1_a5), .A6(s257_01_1_a6), .A7(s257_01_1_a7), .A8(s257_01_1_a8), .A9(s257_01_1_a9),
    .PWR(t_ff_1_q), .CLK(CLK), .ENA(and_13_out), .R_W(RW), .RST(RST), .D0(D0), .D1(D1), .D2(D2), .D3(D3),
    .D4(D4), .D5(D5), .D6(D6), .D7(D7));
  Clock clock_1 (.out(clock_1_out));
  or or_1 (or_1_out, PWR, and_1_out);
  and and_1 (and_1_out, s257_01_1_stp, t_ff_1_q);
  T_Flip_Flop t_ff_1 (.clk(or_1_out), .T(or_1_out), .Q(t_ff_1_q));  // open: Qn, preset, reset
  and and_2 (and_2_out, s257_01_1_a15, t_ff_1_q);
  and and_3 (and_3_out, t_ff_1_q, not_1_out);
  not not_1 (not_1_out, s257_01_1_a15);
  and and_4 (and_4_out, s257_01_1_a14, and_3_out);
  and and_5 (and_5_out, and_3_out, not_2_out);
  not not_2 (not_2_out, s257_01_1_a14);
  and and_6 (and_6_out, s257_01_1_a13, and_5_out);
  and and_7 (and_7_out, and_5_out, not_3_out);
  not not_3 (not_3_out, s257_01_1_a13);
  and and_8 (and_8_out, s257_01_1_a12, and_7_out);
  and and_9 (and_9_out, and_7_out, not_4_out);
  not not_4 (not_4_out, s257_01_1_a12);
  and and_10 (and_10_out, s257_01_1_a11, and_8_out);
  and and_11 (and_11_out, and_8_out, not_5_out);
  not not_5 (not_5_out, s257_01_1_a11);
  and and_12 (and_12_out, s257_01_1_a10, and_10_out);
  and and_13 (and_13_out, and_10_out, not_6_out);
  not not_6 (not_6_out, s257_01_1_a10);
  and and_14 (and_14_out, s257_01_1_a9, and_12_out);
  and and_15 (and_15_out, and_12_out, not_7_out);
  not not_7 (not_7_out, s257_01_1_a9);
  and and_16 (and_16_out, s257_01_1_a8, and_15_out);
  and and_17 (and_17_out, and_15_out, not_8_out);
  not not_8 (not_8_out, s257_01_1_a8);
  states states_1 (
    .E_VPU(states_1_e_vpu), .E(and_17_out), .C_ROM2(rom_2k_1_gnd), .C_RAM(ram_1k_1_gnd),
    .C_RAM16(ram_16k_1_gnd), .C_VRAM(ram_8k_1_gnd), .C_EXT(ext_1_gnd_2), .C_ROM4(rom_4k_1_gnd));  // open: D1, D2, D3, D4, D5, D6, D7, E_FDC, E_IO, D0, A0, A1, A2, A3, A4, C_MEM, C_IO
  vpu vpu_1 (
    .VRAM(vpu_1_vram), .STATE(states_1_e_vpu));  // open: VIDEO, GND, S0_2, S1_2, S2_2, D1_2, D2_2, D3_2, D4_2, D5_2, D6_2, D7_2, D0_2, RST, PWR, CLK, R_W, S0, S1, S2, D0, D1, D2, D3, D4, D5, D6, D7, A0, A1, A2, A3, A4, A5, A6, A7, A8, A9, A10, A11, A12

  // Notes on the sheet:
  //   EXT
  //   RAM
  //   VRAM
  //   ROM4
  //   ROM2
  //   RAM1
  //   MEM
  //   STATES
  //   IO
endmodule

module S257_01 (
  input  D0,
  input  D1,
  input  D2,
  input  D3,
  input  D4,
  input  D5,
  input  D6,
  input  D7,
  input  CLK,
  input  PWR,
  output A0,
  output A1,
  output A2,
  output A3,
  output A4,
  output A5,
  output STP,
  output RST,
  output A6,
  output D0_2,
  output A7,
  output D1_2,
  output A8,
  output D2_2,
  output A9,
  output R_W,
  output D3_2,
  output A10,
  output D4_2,
  output A11,
  output D5_2,
  output A12,
  output D6_2,
  output A13,
  output D7_2,
  output A14,
  output A15,
  output CLK_2,
  output GND
);

  wire and_1_out, and_3_out, and_4_out, and_5_out, and_7_out, and_8_out, and_11_out, and_16_out, and_17_out,
       and_18_out, and_19_out, and_20_out, and_21_out, and_23_out, buffer_1_out, buffer_2_out, buffer_3_out,
       buffer_4_out, buffer_5_out, buffer_6_out, CLK_t, cu_1_s, decoder_1_out0, decoder_1_out1,
       decoder_1_out2, decoder_1_out3, EB, ECU, EJ, ER, ERA, ERB, ERC, ERD, ERE, ERF, ERG0, ERG1, ERG2, ERG3,
       ERG4, ERG5, ERJ1, ERJ2, ERR, EWJ, F, G, J, JB, nor_1_out, not_1_out, not_2_out, not_3_out, not_4_out,
       not_5_out, not_6_out, not_7_out, not_8_out, not_9_out, not_10_out, not_11_out, or_1_out, or_3_out,
       or_4_out, or_5_out, or_6_out, or_7_out, or_8_out, or_9_out, or_10_out, or_11_out, or_12_out,
       or_13_out, or_14_out, or_15_out, or_16_out, or_17_out, or_18_out, PC, RST_t, VA, VB, VD, xor_1_out,
       xor_2_out, xor_3_out, xor_4_out, xor_5_out, xor_6_out, xor_7_out, xor_8_out;
  wire [3:0] alu_8b_1_legc, SEL, STP_q;
  wire [4:0] cu_1_alu;
  wire [7:0] A, alu_8b_1_s, B, controlled_buffer_4_out, D, demultiplexer_1_out6, demultiplexer_1_out8,
       demultiplexer_1_out9, IN, multiplexer_1_out, multiplexer_2_out, multiplexer_3_out, OP1, OP2, OP3, OP4,
       RAI, RAO, RBI, RBO, RCI, RCO, RDI, RDO, REI, REO, RFI, RFO, RG0I, RG0O, RG1I, RG1O, RG2I, RG2O, RG3I,
       RG3O, RG4I, RG4O, RG5I, RG5O, RJ1I, RJ1O, RJ2I, RJ2O, RRO;
  wire [15:0] controlled_buffer_16_out, register_1_q;

  assign {D7_2, D6_2, D5_2, D4_2, D3_2, D2_2, D1_2, D0_2} = R_W ? D : 8'bz;  // Controlled_Buffer controlled_buffer_1
  Pull_Resistor pull_resistor_1 (.node(STP));
  Pull_Resistor pull_resistor_2 (.node(RST));
  assign IN = not_1_out ? {D7, D6, D5, D4, D3, D2, D1, D0} : 8'bz;  // Controlled_Buffer controlled_buffer_2
  Register #(.trigger("falling")) u_OP1 (.D(IN), .Q(OP1), .clk(and_1_out), .clr(RST_t));  // open: en
  and and_1 (and_1_out, decoder_1_out0, not_4_out);
  Decoder #(.enable("false"), .select(2)) decoder_1 (
    .out0(decoder_1_out0), .out1(decoder_1_out1), .out2(decoder_1_out2), .out3(decoder_1_out3),
    .sel(STP_q[1:0]));
  Counter #(.max('hf), .width(4)) u_STP (.count(CLK_t), .Q(STP_q), .clk(CLK_t), .clr(RST_t));  // open: load, D, carry
  and and_2 (CLK_t, CLK, buffer_3_out);
  or or_1 (or_1_out, RST, PWR);
  Decoder #(.select(4)) decoder_2 (
    .out1(ERA), .out2(ERB), .out3(ERC), .out4(ERD), .out5(ERE), .out6(ERF), .out7(ERR), .out8(ERJ1),
    .out9(ERJ2), .out10(ERG0), .out11(ERG1), .out12(ERG2), .out13(ERG3), .out14(ERG4), .out15(ERG5),
    .sel(SEL), .en(ER));  // open: out0
  alu_8b alu_8b_1 (.S(alu_8b_1_s), .LEGC(alu_8b_1_legc), .OP(cu_1_alu), .A(A), .B(B));
  cu cu_1 (
    .RST(RST), .OFF(STP), .ALU(cu_1_alu), .A(VA), .B(VB), .S(cu_1_s), .J(J), .GET(G), .SET(R_W), .F(F),
    .D(VD), .OP(OP1), .E(ECU));
  Register #(.trigger("falling")) u_OP2 (.D(IN), .Q(OP2), .clk(and_3_out), .clr(RST_t));  // open: en
  and and_3 (and_3_out, decoder_1_out1, not_4_out);
  and and_4 (and_4_out, STP_q[2], not_1_out);
  and and_5 (and_5_out, ~STP_q[2], STP_q[3]);  // AND_Gate
  not not_1 (not_1_out, STP_q[3]);
  not not_2 (not_2_out, or_1_out);
  and and_6 (RST_t, not_2_out, or_1_out);
  buf buffer_1 (buffer_1_out, PWR);
  buf buffer_2 (buffer_2_out, buffer_1_out);
  buf buffer_3 (buffer_3_out, buffer_2_out);
  assign RFI = F ? {4'b0000, alu_8b_1_legc} : 8'bz;  // Controlled_Buffer controlled_buffer_3
  assign controlled_buffer_4_out = not_3_out ? alu_8b_1_s : 8'bz;  // Controlled_Buffer controlled_buffer_4
  Demultiplexer #(.enable("false"), .select(4), .width(8)) demultiplexer_1 (
    .out1(RAI), .out2(RBI), .out3(RCI), .out4(RDI), .out5(REI), .out6(demultiplexer_1_out6),
    .out8(demultiplexer_1_out8), .out9(demultiplexer_1_out9), .out10(RG0I), .out11(RG1I), .out12(RG2I),
    .out13(RG3I), .out14(RG4I), .out15(RG5I), .in(controlled_buffer_4_out), .sel(SEL));  // open: out0, out7
  Pull_Resistor pull_resistor_3 (.node(controlled_buffer_4_out));
  not not_3 (not_3_out, G);
  assign controlled_buffer_4_out = G ? IN : 8'bz;  // Controlled_Buffer controlled_buffer_5
  Register #(.trigger("falling")) u_OP3 (.D(IN), .Q(OP3), .clk(and_7_out), .clr(RST_t));  // open: en
  and and_7 (and_7_out, decoder_1_out2, not_4_out);
  and and_8 (and_8_out, decoder_1_out3, not_4_out);
  not not_4 (not_4_out, STP_q[2]);
  or or_2 (ECU, and_4_out, and_5_out);
  and and_9 (PC, ~STP_q[2], not_1_out);  // AND_Gate
  and and_10 (CLK_2, not_1_out, buffer_3_out);
  assign RJ1I = not_5_out ? demultiplexer_1_out8 : 8'bz;  // Controlled_Buffer controlled_buffer_6
  not not_5 (not_5_out, JB);
  assign RJ2I = not_5_out ? demultiplexer_1_out9 : 8'bz;  // Controlled_Buffer controlled_buffer_7
  Pull_Resistor pull_resistor_4 (.node(SEL));
  assign SEL = not_6_out ? OP2[3:0] : 4'bz;  // Controlled_Buffer controlled_buffer_8
  not not_6 (not_6_out, cu_1_s);
  Register #(.trigger("falling")) u_OP4 (.D(IN), .Q(OP4), .clk(and_8_out), .clr(RST_t));  // open: en
  or or_3 (or_3_out, G, R_W);
  and and_11 (and_11_out, and_5_out, decoder_1_out0);
  and and_12 (EJ, decoder_1_out0, and_4_out);
  and and_13 (ER, and_4_out, decoder_1_out2);
  and and_14 (EWJ, and_4_out, decoder_1_out1);
  not not_7 (not_7_out, F);
  assign RFI = not_7_out ? demultiplexer_1_out6 : 8'bz;  // Controlled_Buffer controlled_buffer_9
  and and_15 (EB, or_3_out, and_11_out);
  or or_4 (or_4_out, EWJ, ER);
  or or_5 (or_5_out, G, R_W);
  and and_16 (and_16_out, ~or_5_out, JB);  // AND_Gate
  Multiplexer #(.enable("false"), .select(4), .width(8)) multiplexer_1 (
    .in0({8{1'b0}}), .in1(RAO), .in2(RBO), .in3(RCO), .in4(RDO), .in5(REO), .in6(RFO), .in7(RRO), .in8(RJ1O),
    .in9(RJ2O), .in10(RG0O), .in11(RG1O), .in12(RG2O), .in13(RG3O), .in14(RG4O), .in15(RG5O),
    .out(multiplexer_1_out), .sel(OP4[3:0]));
  Multiplexer #(.enable("false"), .select(4), .width(8)) multiplexer_2 (
    .in0({8{1'b0}}), .in1(RAO), .in2(RBO), .in3(RCO), .in4(RDO), .in5(REO), .in6(RFO), .in7(RRO), .in8(RJ1O),
    .in9(RJ2O), .in10(RG0O), .in11(RG1O), .in12(RG2O), .in13(RG3O), .in14(RG4O), .in15(RG5O),
    .out(multiplexer_2_out), .sel(OP3[3:0]));
  Multiplexer #(.enable("false"), .select(4), .width(8)) multiplexer_3 (
    .in0({8{1'b0}}), .in1(RAO), .in2(RBO), .in3(RCO), .in4(RDO), .in5(REO), .in6(RFO), .in7(RRO), .in8(RJ1O),
    .in9(RJ2O), .in10(RG0O), .in11(RG1O), .in12(RG2O), .in13(RG3O), .in14(RG4O), .in15(RG5O),
    .out(multiplexer_3_out), .sel(OP2[3:0]));
  Register u_A (.D(RAI), .en(or_4_out), .Q(RAO), .clk(ERA), .clr(RST_t));
  and and_17 (and_17_out, F, or_4_out);
  or or_6 (or_6_out, and_17_out, ERF);
  and and_18 (and_18_out, and_16_out, or_4_out);
  or or_7 (or_7_out, and_18_out, ERJ1);
  Register G0 (.D(RG0I), .en(or_4_out), .Q(RG0O), .clk(ERG0), .clr(RST_t));
  assign B = not_8_out ? multiplexer_1_out : 8'bz;  // Controlled_Buffer controlled_buffer_10
  Pull_Resistor pull_resistor_5 (.node(B));
  not not_8 (not_8_out, VB);
  assign B = VB ? OP4 : 8'bz;  // Controlled_Buffer controlled_buffer_11
  assign A = not_9_out ? multiplexer_2_out : 8'bz;  // Controlled_Buffer controlled_buffer_12
  Pull_Resistor pull_resistor_6 (.node(A));
  not not_9 (not_9_out, VA);
  assign A = VA ? OP3 : 8'bz;  // Controlled_Buffer controlled_buffer_13
  assign D = not_10_out ? multiplexer_3_out : 8'bz;  // Controlled_Buffer controlled_buffer_14
  Pull_Resistor pull_resistor_7 (.node(D));
  not not_10 (not_10_out, VD);
  assign D = VD ? OP2 : 8'bz;  // Controlled_Buffer controlled_buffer_15
  Register u_B (.D(RBI), .en(or_4_out), .Q(RBO), .clk(ERB), .clr(RST_t));
  Register u_F (.D(RFI), .en(or_4_out), .Q(RFO), .clk(or_6_out), .clr(RST_t));
  Register J1 (.D(RJ1I), .en(or_4_out), .Q(RJ1O), .clk(or_7_out), .clr(RST_t));
  Register G1 (.D(RG1I), .en(or_4_out), .Q(RG1O), .clk(ERG1), .clr(RST_t));
  // Random R: pin names not known; wires that end beside it: or_4_out, CLK_2, RST_t, RRO
  or or_8 (or_8_out, G, R_W);
  and and_19 (and_19_out, ~or_8_out, JB);  // AND_Gate
  and and_20 (and_20_out, and_19_out, or_4_out);
  Register C (.D(RCI), .en(or_4_out), .Q(RCO), .clk(ERC), .clr(RST_t));
  Register J2 (.D(RJ2I), .en(or_4_out), .Q(RJ2O), .clk(or_9_out), .clr(RST_t));
  or or_9 (or_9_out, and_20_out, ERJ2);
  Register G2 (.D(RG2I), .en(or_4_out), .Q(RG2O), .clk(ERG2), .clr(RST_t));
  xor xor_1 (xor_1_out, D[0], RFO[0]);
  or or_10 (or_10_out, xor_1_out, xor_2_out);
  xor xor_2 (xor_2_out, D[1], RFO[1]);
  xor xor_3 (xor_3_out, D[2], RFO[2]);
  or or_11 (or_11_out, xor_3_out, xor_4_out);
  xor xor_4 (xor_4_out, D[3], RFO[3]);
  xor xor_5 (xor_5_out, D[4], RFO[4]);
  or or_12 (or_12_out, xor_5_out, xor_6_out);
  xor xor_6 (xor_6_out, D[5], RFO[5]);
  xor xor_7 (xor_7_out, D[6], RFO[6]);
  or or_13 (or_13_out, xor_7_out, xor_8_out);
  xor xor_8 (xor_8_out, D[7], RFO[7]);
  or or_14 (or_14_out, EJ, EB);
  not not_11 (not_11_out, EB);
  assign controlled_buffer_16_out = not_11_out ? {A, B} : 16'bz;  // Controlled_Buffer controlled_buffer_16
  assign controlled_buffer_16_out = EB ? register_1_q : 16'bz;  // Controlled_Buffer controlled_buffer_17
  Register u_D (.D(RDI), .en(or_4_out), .Q(RDO), .clk(ERD), .clr(RST_t));
  Register G3 (.D(RG3I), .en(or_4_out), .Q(RG3O), .clk(ERG3), .clr(RST_t));
  or or_15 (or_15_out, or_10_out, or_11_out);
  nor nor_1 (nor_1_out, or_15_out, or_16_out);
  or or_16 (or_16_out, or_12_out, or_13_out);
  or or_17 (or_17_out, G, R_W);
  or or_18 (or_18_out, nor_1_out, or_17_out);
  and and_21 (and_21_out, J, or_18_out);
  and and_22 (JB, or_14_out, and_21_out);
  Counter #(.max('hffff), .width(16)) u_PC (
    .load(JB), .D(controlled_buffer_16_out), .count(PC),
    .Q({A15, A14, A13, A12, A11, A10, A9, A8, A7, A6, A5, A4, A3, A2, A1, A0}), .clk(CLK_t), .clr(RST_t));  // open: carry
  Register #(.width(16)) register_1 (
    .D({A15, A14, A13, A12, A11, A10, A9, A8, A7, A6, A5, A4, A3, A2, A1, A0}), .en(and_23_out),
    .Q(register_1_q), .clk(CLK_t), .clr(RST_t));
  and and_23 (and_23_out, JB, EJ);
  buf buffer_4 (buffer_4_out, buffer_6_out);
  buf buffer_5 (buffer_5_out, and_23_out);
  buf buffer_6 (buffer_6_out, buffer_5_out);
  Register E (.D(REI), .en(or_4_out), .Q(REO), .clk(ERE), .clr(RST_t));
  Register G4 (.D(RG4I), .en(or_4_out), .Q(RG4O), .clk(ERG4), .clr(RST_t));
  assign RJ2I = buffer_4_out ? register_1_q[7:0] : 8'bz;  // Controlled_Buffer controlled_buffer_18
  assign RJ1I = buffer_4_out ? register_1_q[15:8] : 8'bz;  // Controlled_Buffer controlled_buffer_19
  Register G5 (.D(RG5I), .en(or_4_out), .Q(RG5O), .clk(ERG5), .clr(RST_t));

  assign GND = PWR;

  // Other names for the same wires on the sheet: CLKL = CLK_2; R = RST; S = R_W
endmodule

module cu (
  input  E,
  input  [7:0] OP,
  output [4:0] ALU,
  output A,
  output B,
  output S,
  output J,
  output GET,
  output SET,
  output F,
  output D,
  output RST,
  output OFF
);

  wire and_1_out, and_2_out, and_3_out, and_4_out, and_5_out, and_6_out, and_7_out, and_8_out, and_9_out;
  wire [7:0] controlled_buffer_1_out;

  and and_1 (and_1_out, ~OP[2], ~OP[3]);  // AND_Gate
  and and_2 (and_2_out, ~OP[4], ~OP[5]);  // AND_Gate
  and and_3 (and_3_out, and_2_out, and_4_out);
  and and_4 (and_4_out, ~OP[6], ~OP[7]);  // AND_Gate
  assign controlled_buffer_1_out = E ? OP : 8'bz;  // Controlled_Buffer controlled_buffer_1
  PLA #(.in_width(8), .out_width(13), .\table ("00000000 0000010000000 # NOP\n00000001 0000000000000 # RST\n00000010 0000000000000 # OFF\n00000011 0000000000000 # MOV_R\n00000100 0000000100000 # MOV_V\n00000101 0100010000011 # CMP_RR\n00000110 0100010100011 # CMP_VR\n00000111 0100011000011 # CMP_RV\n00001000 0100011100011 # CMP_VV\n00010000 0000000000000 # ADD_RR\n00010001 0000000000001 # ADC_RR\n00010010 0000000000011 # SUB_RR\n00010011 0000000000010 # SBB_RR\n00010100 0000000010000 # MUL_RR\n00010101 0000000010100 # DIV_RR\n00010110 0000000011000 # MOD_RR\n00010111 0000000000100 # AND_RR\n00011000 0000000001000 # OR_RR\n00011001 0000000001100 # XOR_RR\n00100000 0000000100000 # ADD_VR\n00100001 0000000100001 # ADC_VR\n00100010 0000000100011 # SUB_VR\n00100011 0000000100010 # SBB_VR\n00100100 0000000110000 # MUL_VR\n00100101 0000000110100 # DIV_VR\n00100110 0000000111000 # MOD_VR\n00100111 0000000100100 # AND_VR\n00101000 0000000101000 # OR_VR\n00101001 0000000101100 # XOR_VR\n00110000 0000001000000 # ADD_RV\n00110001 0000001000001 # ADC_RV\n00110010 0000001000011 # SUB_RV\n00110011 0000001000010 # SBB_RV\n00110100 0000001010000 # MUL_RV\n00110101 0000001010100 # DIV_RV\n00110110 0000001011000 # MOD_RV\n00110111 0000001000100 # AND_RV\n00111000 0000001001000 # OR_RV\n00111001 0000001001100 # XOR_RV\n01000000 0000001100000 # ADD_VV\n01000001 0000001100001 # ADC_VV\n01000010 0000001100011 # SUB_VV\n01000011 0000001100010 # SBB_VV\n01000100 0000001110000 # MUL_VV\n01000101 0000001110100 # DIV_VV\n01000110 0000001111000 # MOD_VV\n01000111 0000001100100 # AND_VV\n01001000 0000001101000 # OR_VV\n01001001 0000001101100 # XOR_VV\n01010000 0000110000000 # JMP_RRR\n01010001 0000110100000 # JMP_RVR\n01010010 0000111000000 # JMP_RRV\n01010011 0000111100000 # JMP_RVV\n01010100 1000110000000 # JMP_VRR\n01010101 1000110100000 # JMP_VVR\n01010110 1000111000000 # JMP_VRV\n01010111 1000111100000 # JMP_VVV\n01100000 0001100000000 # GET_RR\n01100001 0001100100000 # GET_VR\n01100010 0001101000000 # GET_RV\n01100011 0001101100000 # GET_VV\n01100100 0010110000000 # SET_RRR\n01100101 0010110100000 # SET_RVR\n01100110 0010111000000 # SET_RRV\n01100111 0010111100000 # SET_RVV\n01101000 1010110000000 # SET_VRR\n01101001 1010110100000 # SET_VVR\n01101010 1010111000000 # SET_VRV\n01101011 1010111100000 # SET_VVV")) pla_1 (
    .in(controlled_buffer_1_out), .out({D, F, SET, GET, J, S, B, A, ALU}));
  Pull_Resistor pull_resistor_1 (.node(controlled_buffer_1_out));
  and and_5 (and_5_out, and_1_out, and_3_out);
  and and_6 (and_6_out, OP[0], ~OP[1]);  // AND_Gate
  and and_7 (and_7_out, and_5_out, and_6_out);
  assign RST = E ? and_7_out : 1'bz;  // Controlled_Buffer controlled_buffer_2
  and and_8 (and_8_out, ~OP[0], OP[1]);  // AND_Gate
  and and_9 (and_9_out, and_5_out, and_8_out);
  assign OFF = E ? and_9_out : 1'bz;  // Controlled_Buffer controlled_buffer_3
endmodule

module alu_8b (
  input  [7:0] A,
  input  [7:0] B,
  input  [4:0] OP,
  output [3:0] LEGC,
  output [7:0] S
);

  wire alu_1b_1_and, alu_1b_1_or, alu_1b_1_s, alu_1b_1_xor, alu_1b_2_and, alu_1b_2_co, alu_1b_2_or,
       alu_1b_2_s, alu_1b_2_xor, alu_1b_3_and, alu_1b_3_co, alu_1b_3_or, alu_1b_3_s, alu_1b_3_xor,
       alu_1b_4_and, alu_1b_4_co, alu_1b_4_or, alu_1b_4_s, alu_1b_4_xor, alu_1b_5_and, alu_1b_5_co,
       alu_1b_5_or, alu_1b_5_s, alu_1b_5_xor, alu_1b_6_and, alu_1b_6_co, alu_1b_6_or, alu_1b_6_s,
       alu_1b_6_xor, alu_1b_7_and, alu_1b_7_co, alu_1b_7_or, alu_1b_7_s, alu_1b_7_xor, alu_1b_8_and,
       alu_1b_8_co, alu_1b_8_or, alu_1b_8_s, alu_1b_8_xor, and_3_out, and_4_out, nor_1_out, nor_2_out,
       nor_3_out, nor_4_out, xor_1_out;
  wire [7:0] divider_1_out, divider_1_rem, multiplier_1_out;

  xor xor_1 (xor_1_out, LEGC[0], alu_1b_2_co);
  xor xor_2 (LEGC[3], xor_1_out, S[7]);
  and and_1 (LEGC[1], ~LEGC[3], ~LEGC[2]);  // AND_Gate
  alu_1b alu_1b_1 (
    .CO(LEGC[0]), .AND(alu_1b_1_and), .OR(alu_1b_1_or), .XOR(alu_1b_1_xor), .S(alu_1b_1_s), .CI(alu_1b_2_co),
    .A(A[7]), .B(B[7]), .I(OP[1]));
  Multiplexer #(.enable("false"), .select(3)) multiplexer_1 (
    .in0(alu_1b_1_s), .in1(alu_1b_1_and), .in2(alu_1b_1_or), .in3(alu_1b_1_xor), .in4(multiplier_1_out[7]),
    .in5(divider_1_out[7]), .in6(divider_1_rem[7]), .in7(1'b0), .out(S[7]), .sel(OP[4:2]));
  alu_1b alu_1b_2 (
    .CO(alu_1b_2_co), .AND(alu_1b_2_and), .OR(alu_1b_2_or), .XOR(alu_1b_2_xor), .S(alu_1b_2_s),
    .CI(alu_1b_3_co), .A(A[6]), .B(B[6]), .I(OP[1]));
  Multiplexer #(.enable("false"), .select(3)) multiplexer_2 (
    .in0(alu_1b_2_s), .in1(alu_1b_2_and), .in2(alu_1b_2_or), .in3(alu_1b_2_xor), .in4(multiplier_1_out[6]),
    .in5(divider_1_out[6]), .in6(divider_1_rem[6]), .in7(1'b0), .out(S[6]), .sel(OP[4:2]));
  and and_2 (LEGC[2], and_3_out, and_4_out);
  alu_1b alu_1b_3 (
    .CO(alu_1b_3_co), .AND(alu_1b_3_and), .OR(alu_1b_3_or), .XOR(alu_1b_3_xor), .S(alu_1b_3_s),
    .CI(alu_1b_4_co), .A(A[5]), .B(B[5]), .I(OP[1]));
  Multiplexer #(.enable("false"), .select(3)) multiplexer_3 (
    .in0(alu_1b_3_s), .in1(alu_1b_3_and), .in2(alu_1b_3_or), .in3(alu_1b_3_xor), .in4(multiplier_1_out[5]),
    .in5(divider_1_out[5]), .in6(divider_1_rem[5]), .in7(1'b0), .out(S[5]), .sel(OP[4:2]));
  and and_3 (and_3_out, nor_1_out, nor_2_out);
  and and_4 (and_4_out, nor_3_out, nor_4_out);
  alu_1b alu_1b_4 (
    .CO(alu_1b_4_co), .AND(alu_1b_4_and), .OR(alu_1b_4_or), .XOR(alu_1b_4_xor), .S(alu_1b_4_s),
    .CI(alu_1b_5_co), .A(A[4]), .B(B[4]), .I(OP[1]));
  nor nor_1 (nor_1_out, S[0], S[1]);
  nor nor_2 (nor_2_out, S[2], S[3]);
  nor nor_3 (nor_3_out, S[4], S[5]);
  nor nor_4 (nor_4_out, S[6], S[7]);
  Multiplexer #(.enable("false"), .select(3)) multiplexer_4 (
    .in0(alu_1b_4_s), .in1(alu_1b_4_and), .in2(alu_1b_4_or), .in3(alu_1b_4_xor), .in4(multiplier_1_out[4]),
    .in5(divider_1_out[4]), .in6(divider_1_rem[4]), .in7(1'b0), .out(S[4]), .sel(OP[4:2]));
  alu_1b alu_1b_5 (
    .CO(alu_1b_5_co), .AND(alu_1b_5_and), .OR(alu_1b_5_or), .XOR(alu_1b_5_xor), .S(alu_1b_5_s),
    .CI(alu_1b_6_co), .A(A[3]), .B(B[3]), .I(OP[1]));
  Multiplexer #(.enable("false"), .select(3)) multiplexer_5 (
    .in0(alu_1b_5_s), .in1(alu_1b_5_and), .in2(alu_1b_5_or), .in3(alu_1b_5_xor), .in4(multiplier_1_out[3]),
    .in5(divider_1_out[3]), .in6(divider_1_rem[3]), .in7(1'b0), .out(S[3]), .sel(OP[4:2]));
  alu_1b alu_1b_6 (
    .CO(alu_1b_6_co), .AND(alu_1b_6_and), .OR(alu_1b_6_or), .XOR(alu_1b_6_xor), .S(alu_1b_6_s),
    .CI(alu_1b_7_co), .A(A[2]), .B(B[2]), .I(OP[1]));
  Multiplexer #(.enable("false"), .select(3)) multiplexer_6 (
    .in0(alu_1b_6_s), .in1(alu_1b_6_and), .in2(alu_1b_6_or), .in3(alu_1b_6_xor), .in4(multiplier_1_out[2]),
    .in5(divider_1_out[2]), .in6(divider_1_rem[2]), .in7(1'b0), .out(S[2]), .sel(OP[4:2]));
  alu_1b alu_1b_7 (
    .CO(alu_1b_7_co), .AND(alu_1b_7_and), .OR(alu_1b_7_or), .XOR(alu_1b_7_xor), .S(alu_1b_7_s),
    .CI(alu_1b_8_co), .A(A[1]), .B(B[1]), .I(OP[1]));
  Multiplexer #(.enable("false"), .select(3)) multiplexer_7 (
    .in0(alu_1b_7_s), .in1(alu_1b_7_and), .in2(alu_1b_7_or), .in3(alu_1b_7_xor), .in4(multiplier_1_out[1]),
    .in5(divider_1_out[1]), .in6(divider_1_rem[1]), .in7(1'b0), .out(S[1]), .sel(OP[4:2]));
  alu_1b alu_1b_8 (
    .CO(alu_1b_8_co), .AND(alu_1b_8_and), .OR(alu_1b_8_or), .XOR(alu_1b_8_xor), .S(alu_1b_8_s), .CI(OP[0]),
    .A(A[0]), .B(B[0]), .I(OP[1]));
  Multiplexer #(.enable("false"), .select(3)) multiplexer_8 (
    .in0(alu_1b_8_s), .in1(alu_1b_8_and), .in2(alu_1b_8_or), .in3(alu_1b_8_xor), .in4(multiplier_1_out[0]),
    .in5(divider_1_out[0]), .in6(divider_1_rem[0]), .in7(1'b0), .out(S[0]), .sel(OP[4:2]));
  Multiplier multiplier_1 (.a(A), .b(B), .out(multiplier_1_out));  // open: cin, cout
  Divider divider_1 (.a(A), .b(B), .out(divider_1_out), .rem(divider_1_rem));  // open: upper
endmodule

module alu_1b (
  input  A,
  input  B,
  input  I,
  input  CI,
  output XOR,
  output S,
  output CO,
  output AND,
  output OR
);

  wire and_1_out, xor_1_out;

  xor xor_1 (xor_1_out, B, I);
  xor xor_2 (XOR, A, xor_1_out);
  xor xor_3 (S, XOR, CI);
  and and_1 (and_1_out, CI, XOR);
  or or_1 (CO, and_1_out, AND);
  and and_2 (AND, A, xor_1_out);
  or or_2 (OR, A, xor_1_out);
endmodule

module ram_16k (
  input  A0,
  input  A1,
  input  R_W,
  input  A2,
  input  PWR,
  input  A3,
  input  CLK,
  input  ENA,
  input  A4,
  input  A5,
  input  D0,
  input  A6,
  input  D1,
  input  A7,
  input  D2,
  input  A8,
  input  D3,
  input  A9,
  input  RST,
  input  D4,
  input  A10,
  input  D5,
  input  A11,
  input  D6,
  input  A12,
  input  D7,
  input  A13,
  output D0_2,
  output D1_2,
  output D2_2,
  output D3_2,
  output D4_2,
  output GND,
  output D5_2,
  output D6_2,
  output D7_2
);

  wire and_1_out, and_2_out, and_3_out, and_4_out;
  wire [7:0] controlled_buffer_2_out, ram_1_dout;

  and and_1 (and_1_out, ~R_W, ENA);  // AND_Gate
  and and_2 (and_2_out, PWR, CLK);
  and and_3 (and_3_out, R_W, ENA);
  RAM #(.addrWidth(14), .trigger("falling")) ram_1 (
    .addr({A13, A12, A11, A10, A9, A8, A7, A6, A5, A4, A3, A2, A1, A0}), .we(R_W), .clk(and_4_out),
    .din(controlled_buffer_2_out), .dout(ram_1_dout));
  and and_4 (and_4_out, and_2_out, ENA);
  assign {D7_2, D6_2, D5_2, D4_2, D3_2, D2_2, D1_2, D0_2} = and_1_out ? ram_1_dout : 8'bz;  // Controlled_Buffer controlled_buffer_1
  assign controlled_buffer_2_out = and_3_out ? {D7, D6, D5, D4, D3, D2, D1, D0} : 8'bz;  // Controlled_Buffer controlled_buffer_2

  assign GND = PWR;
endmodule

module ram_8k (
  input  A0,
  input  A1,
  input  R_W,
  input  A2,
  input  PWR,
  input  A3,
  input  CLK,
  input  ENA,
  input  A4,
  input  A5,
  input  D0,
  input  A6,
  input  D1,
  input  A7,
  input  D2,
  input  A8,
  input  D3,
  input  A9,
  input  RST,
  input  D4,
  input  A10,
  input  D5,
  input  A11,
  input  D6,
  input  A12,
  input  D7,
  output D0_2,
  output D1_2,
  output D2_2,
  output D3_2,
  output D4_2,
  output GND,
  output D5_2,
  output D6_2,
  output D7_2
);

  wire and_1_out, and_2_out, and_3_out, and_4_out;
  wire [7:0] controlled_buffer_2_out, ram_1_dout;

  and and_1 (and_1_out, ~R_W, ENA);  // AND_Gate
  and and_2 (and_2_out, PWR, CLK);
  and and_3 (and_3_out, R_W, ENA);
  RAM #(.addrWidth(13), .trigger("falling")) ram_1 (
    .addr({A12, A11, A10, A9, A8, A7, A6, A5, A4, A3, A2, A1, A0}), .we(R_W), .clk(and_4_out),
    .din(controlled_buffer_2_out), .dout(ram_1_dout));
  and and_4 (and_4_out, and_2_out, ENA);
  assign {D7_2, D6_2, D5_2, D4_2, D3_2, D2_2, D1_2, D0_2} = and_1_out ? ram_1_dout : 8'bz;  // Controlled_Buffer controlled_buffer_1
  assign controlled_buffer_2_out = and_3_out ? {D7, D6, D5, D4, D3, D2, D1, D0} : 8'bz;  // Controlled_Buffer controlled_buffer_2

  assign GND = PWR;
endmodule

module ram_1k (
  input  A0,
  input  A1,
  input  R_W,
  input  A2,
  input  PWR,
  input  A3,
  input  CLK,
  input  ENA,
  input  A4,
  input  A5,
  input  D0,
  input  A6,
  input  D1,
  input  A7,
  input  D2,
  input  A8,
  input  D3,
  input  A9,
  input  RST,
  input  D4,
  input  D5,
  input  D6,
  input  D7,
  output D0_2,
  output D1_2,
  output D2_2,
  output D3_2,
  output D4_2,
  output GND,
  output D5_2,
  output D6_2,
  output D7_2
);

  wire and_1_out, and_2_out, and_3_out, and_4_out;
  wire [7:0] controlled_buffer_2_out, ram_1_dout;

  and and_1 (and_1_out, ~R_W, ENA);  // AND_Gate
  and and_2 (and_2_out, PWR, CLK);
  and and_3 (and_3_out, R_W, ENA);
  RAM #(.addrWidth(10), .trigger("falling")) ram_1 (
    .addr({A9, A8, A7, A6, A5, A4, A3, A2, A1, A0}), .we(R_W), .clk(and_4_out),
    .din(controlled_buffer_2_out), .dout(ram_1_dout));
  and and_4 (and_4_out, and_2_out, ENA);
  assign {D7_2, D6_2, D5_2, D4_2, D3_2, D2_2, D1_2, D0_2} = and_1_out ? ram_1_dout : 8'bz;  // Controlled_Buffer controlled_buffer_1
  assign controlled_buffer_2_out = and_3_out ? {D7, D6, D5, D4, D3, D2, D1, D0} : 8'bz;  // Controlled_Buffer controlled_buffer_2

  assign GND = PWR;
endmodule

module rom_4k (
  input  A0,
  input  A1,
  input  A2,
  input  A3,
  input  A4,
  input  A5,
  input  A6,
  input  A7,
  input  R_W,
  input  CLK,
  input  A8,
  input  A9,
  input  ENA,
  input  A10,
  input  PWR,
  input  A11,
  output D0,
  output D1,
  output D2,
  output D3,
  output GND,
  output D4,
  output D5,
  output D6,
  output D7
);

  wire and_1_out;
  wire [7:0] rom_1_data;

  ROM #(.addrWidth(12)) rom_1 (.addr({A11, A10, A9, A8, A7, A6, A5, A4, A3, A2, A1, A0}), .data(rom_1_data));
  and and_1 (and_1_out, ENA, PWR);
  assign {D7, D6, D5, D4, D3, D2, D1, D0} = and_1_out ? rom_1_data : 8'bz;  // Controlled_Buffer controlled_buffer_1

  assign GND = PWR;

  // Notes on the sheet:
  //   contents of rom_1 (hex, n*v repeats v):
  //   compressed eJyVmUGWrCgQReesgnGPBCSA5aCm+19CExAEIGh3ncpzKis+efN5RQz81kiQmzyl3dIbL4NQl3RH
  //   Knm5/7PJHX8E/sZh+FvJGHNBywPHmVTRqeDSe4Ul49JYEPdPWpOGpREnvkufFwZxNn1kGyoN7T2h
  //   vccxiBSaiJKJAurnpfWZaMVYQXQHwnpCL0ieP+cKCcRYKSSfAfiaji7w0YVydL4dXeiPzlAmJZWS
  //   JZxGcYocZoNGGDOnPH3NdG75O9TWYp5bd8CGVSqVChrZWqc/3+E3k35Fge7gP/8ONxT8PbkSipIr
  //   PMx87hlOpQc8M9NJJ6hkKCtXPKFUnVD7Vp2rcUa9Olej831ODpwcyLlqyeHLuXo4X8ADk/zTOZXe
  //   nKuH8wX84OTH7PxYJFdP5/vs/GLn1+z8WjtPwOI8T1elB+dquhq1oODlY8m4rrlL5emEwFoX4V9k
  //   wyBNwju2XgvPQ0xJrbYPuOXcloR3cLtIXgKLCpUMZeHpWEi4Fo6E6yqcSv8p3IzC1Zw8cvJIyk1L
  //   Hr+cm4fzBfxi0knOO/j55dw8nC/gNye/yXkHvxfJzdO5ejpPNXKevpKc862KSrNzR1rwxqH2wbiO
  //   z9xG7JTb4AWUje81N5Vm44jWWHCfaMccIN8dGta+HeouqeEDHTh1INsdOixS57SCkJKRneuDXR/k
  //   em+uj9G1IteRhOCpVnZcwufQPw79I9W2hf6tVSNZIzm+k3ecRBmzSxLN4FKZPWPLZEpi8841vlIM
  //   ae7AZpE4JxWmrttPywlBlndhybKtlqk0z+jBMoxryJzZc2ZPlqGT8WEZBssL8sGYSJo7cvzwDIPn
  //   BfnizBd57sjXIjMMnqeVY5c3e77JMzTP98tqXUUrvAqVG9eOZ2orNKXGbqGYdjU1lRaLNQ7RrlyD
  //   H2zLoJ1cd+z9Za3OskvslP6V7Ti3I9sd2y1yl7iiMuV0d7Tcddvade+u+rZvbffDtx/Xj3sOfnLw
  //   2nb7FnzZdlfhfhS+gt9Mqm13B39pu4txPxqf4cBtN3DbzXBYtt3+oZyh7By47QZuu3mrA29t98N5
  //   GJ1fc3Lg5LXtDi35su2uzsPD+QIemFTb7g7+0nYX5+HhfAE/OHltuzv4qu0OT+fX7Pxi57XtDs35
  //   NW6ex315Owv4s5UNfuo/8oF4uq4Cb9y353c7SV/tRGqLcFDaTM+DUl/SRuWtOO8LqPQesDxasCoP
  //   oWCCgkkKJranaceLlcMJkZMJP4+qM8nVmWR5A+fGmYTJZE3WnSGr/6ossI24vzuLZzcqJ9PNWfw6
  //   qbY8V/hDoosT/T4S/c5uVE5kWqLfn6ZZfuLz/xN6brq90K/zzGOT2kblhNwuUuk/55lt/eT/mWee
  //   HzN5vEu9zDPPtzdfb2+WmzY/3t5e5xn81VlkG8frWfXcYvvaYltozo7PeYbMP8wzL3+c6P5IdJ/d
  //   qJzItUQvbVJd5fGUwfisTE3LcOAuKdQuCfjpR3jrkjJa5cIX2jKHmiRQYizNtw/8GzR5fEc7Tk2T
  //   CHRDL3okMNmQrx3pdOsI3CKF2iIBX9NUUtgENQPIBryqoOy5NH4ij/F0jcD0tClwkxRqkwR7S34+
  //   6HgJQt4G+RXezvibWdQmgRVjSZW2LPNx9kBu/5OaCQ9PfORGKdZGCXgnQKX0FtsLyH0uwghL7lX+
  //   l9F95FYp1lYJeJ5T6eE+3azSC2f2hJ8uo4gniFi2LIbgGz6XdL5qIeBr7TrMMjzLoK0chCbDb801
  //   RHyplYxppx/5dhfr7Q5iS5tKcOBr7Xb674QoT8adhDsa7sRnQ/8C81xTow==
endmodule

module rom_2k (
  input  A0,
  input  A1,
  input  A2,
  input  A3,
  input  A4,
  input  A5,
  input  A6,
  input  R_W,
  input  CLK,
  input  A7,
  input  A8,
  input  ENA,
  input  A9,
  input  PWR,
  input  A10,
  output D0,
  output D1,
  output D2,
  output D3,
  output GND,
  output D4,
  output D5,
  output D6,
  output D7
);

  wire and_1_out;
  wire [7:0] rom_1_data;

  ROM #(.addrWidth(11)) rom_1 (.addr({A10, A9, A8, A7, A6, A5, A4, A3, A2, A1, A0}), .data(rom_1_data));
  and and_1 (and_1_out, ENA, PWR);
  assign {D7, D6, D5, D4, D3, D2, D1, D0} = and_1_out ? rom_1_data : 8'bz;  // Controlled_Buffer controlled_buffer_1

  assign GND = PWR;

  // Notes on the sheet:
  //   contents of rom_1 (hex, n*v repeats v):
  //   4 1 0 0 4 2 ff 0 5 0 1 2 53 6 0 c
endmodule

module vpu (
  input  A0,
  input  A1,
  input  RST,
  input  A2,
  input  A3,
  input  A4,
  input  A5,
  input  PWR,
  input  A6,
  input  CLK,
  input  A7,
  input  STATE,
  input  A8,
  input  R_W,
  input  A9,
  input  S0,
  input  D0,
  input  A10,
  input  S1,
  input  D1,
  input  A11,
  input  S2,
  input  D2,
  input  A12,
  input  D3,
  input  D4,
  input  D5,
  input  D6,
  input  D7,
  output D0_2,
  output VIDEO,
  output D1_2,
  output D2_2,
  output D3_2,
  output D4_2,
  output VRAM,
  output S0_2,
  output D5_2,
  output S1_2,
  output D6_2,
  output S2_2,
  output D7_2,
  output GND
);

  wire and_1_out, and_2_out, and_3_out, and_4_out, and_5_out, and_6_out, undriven;

  and and_1 (and_1_out, PWR, CLK);
  and and_2 (and_2_out, and_1_out, STATE);
  and and_3 (and_3_out, R_W, and_2_out);
  and and_4 (and_4_out, ~R_W, and_2_out);  // AND_Gate
  Controlled_Buffer #(.width(3)) controlled_buffer_1 (.in({S2, S1, S0}), .en(and_4_out));  // open: out
  Controlled_Buffer #(.width(3)) controlled_buffer_2 (.out({S2_2, S1_2, S0_2}), .en(and_3_out));  // open: in
  and and_5 (and_5_out, undriven, and_1_out);
  and and_6 (and_6_out, ~undriven, and_1_out);  // AND_Gate
  Controlled_Buffer #(.width(8)) controlled_buffer_3 (
    .out({D7_2, D6_2, D5_2, D4_2, D3_2, D2_2, D1_2, D0_2}), .en(and_5_out));  // open: in
  Controlled_Buffer #(.width(8)) controlled_buffer_4 (
    .in({D7, D6, D5, D4, D3, D2, D1, D0}), .en(and_6_out));  // open: out
  Counter #(.max('h1fff), .width(13)) counter_1 (
    .Q({A12, A11, A10, A9, A8, A7, A6, A5, A4, A3, A2, A1, A0}), .clr(RST));  // open: load, D, count, carry, clk

  assign GND = PWR;
  assign VRAM = 1'b0;
endmodule

module io (
  input  D0,
  input  D_0,
  input  D1,
  input  D_1,
  input  D2,
  input  D_2,
  input  D3,
  input  D_3,
  input  D4,
  input  D_4,
  input  D5,
  input  D_5,
  input  D6,
  input  D_6,
  input  D7,
  input  D_7,
  input  PWR,
  input  RST,
  input  R_W,
  input  CLK,
  output D0_2,
  output A0,
  output D_0_2,
  output D1_2,
  output A1,
  output D_1_2,
  output D2_2,
  output A2,
  output D_2_2,
  output D3_2,
  output A3,
  output D_3_2,
  output D4_2,
  output A4,
  output D_4_2,
  output D5_2,
  output A5,
  output D_5_2,
  output D6_2,
  output A6,
  output D_6_2,
  output D7_2,
  output D_7_2,
  output GND
);


  assign D0_2 = D0;
endmodule

module states (
  input  C_ROM4,
  input  C_ROM2,
  input  C_RAM,
  input  C_RAM16,
  input  C_VRAM,
  input  C_MEM,
  input  C_IO,
  input  C_EXT,
  input  E,
  input  A0,
  input  A1,
  input  A2,
  input  A3,
  input  A4,
  output D0,
  output D1,
  output D2,
  output D3,
  output D4,
  output D5,
  output D6,
  output D7,
  output E_FDC,
  output E_IO,
  output E_VPU
);

  wire and_1_out, and_2_out, and_3_out, and_4_out, and_5_out, and_6_out;

  Pull_Resistor pull_resistor_1 (.node(C_ROM4));
  Pull_Resistor pull_resistor_2 (.node(C_ROM2));
  Pull_Resistor pull_resistor_3 (.node(C_RAM));
  Pull_Resistor pull_resistor_4 (.node(C_RAM16));
  Pull_Resistor pull_resistor_5 (.node(C_EXT));
  Pull_Resistor pull_resistor_6 (.node(C_IO));
  Pull_Resistor pull_resistor_7 (.node(C_MEM));
  Pull_Resistor pull_resistor_8 (.node(C_VRAM));
  and and_1 (and_1_out, ~A0, ~A1);  // AND_Gate
  and and_2 (and_2_out, and_1_out, ~A2);  // AND_Gate
  and and_3 (and_3_out, A3, ~A4);  // AND_Gate
  and and_4 (and_4_out, ~A3, A4);  // AND_Gate
  and and_5 (and_5_out, A3, A4);
  assign D0 = and_6_out ? C_ROM4 : 1'bz;  // Controlled_Buffer controlled_buffer_1
  assign D1 = and_6_out ? C_ROM2 : 1'bz;  // Controlled_Buffer controlled_buffer_2
  assign D2 = and_6_out ? C_RAM : 1'bz;  // Controlled_Buffer controlled_buffer_3
  assign D3 = and_6_out ? C_RAM16 : 1'bz;  // Controlled_Buffer controlled_buffer_4
  assign D4 = and_6_out ? C_VRAM : 1'bz;  // Controlled_Buffer controlled_buffer_5
  assign D5 = and_6_out ? C_MEM : 1'bz;  // Controlled_Buffer controlled_buffer_6
  assign D6 = and_6_out ? C_IO : 1'bz;  // Controlled_Buffer controlled_buffer_7
  assign D7 = and_6_out ? C_EXT : 1'bz;  // Controlled_Buffer controlled_buffer_8
  and and_6 (and_6_out, E, and_2_out);
  and and_7 (E_FDC, E, and_3_out);
  and and_8 (E_IO, E, and_4_out);
  and and_9 (E_VPU, E, and_5_out);
endmodule

module ext (
  input  D_CPU_0,
  input  D_CPU_1,
  input  D_CPU_2,
  input  A_CPU_0,
  input  D_CPU_3,
  input  A_CPU_1,
  input  PWR,
  input  D_CPU_4,
  input  GND,
  input  A_CPU_2,
  input  D_CPU_5,
  input  CLK,
  input  A_CPU_3,
  input  RST,
  input  D_CPU_6,
  input  A_CPU_4,
  input  D_CPU_7,
  input  A_CPU_5,
  input  A_CPU_6,
  input  R_W,
  input  ENA,
  input  A_CPU_7,
  input  A_CPU_8,
  input  D0,
  input  A_CPU_9,
  input  D1,
  input  A_CPU_10,
  input  D2,
  input  A_CPU_11,
  input  D3,
  input  A_CPU_12,
  input  D4,
  input  A_CPU_13,
  input  D5,
  input  A_CPU_14,
  input  D6,
  input  D7,
  output D0_2,
  output D1_2,
  output D2_2,
  output A0,
  output D3_2,
  output A1,
  output PWR_2,
  output D4_2,
  output GND_2,
  output A2,
  output D5_2,
  output CLK_2,
  output A3,
  output RST_2,
  output D6_2,
  output A4,
  output D7_2,
  output A5,
  output A6,
  output R_W_2,
  output ENA_2,
  output A7,
  output A8,
  output D_CPU_0_2,
  output A9,
  output D_CPU_1_2,
  output A10,
  output D_CPU_2_2,
  output A11,
  output D_CPU_3_2,
  output A12,
  output D_CPU_4_2,
  output A13,
  output D_CPU_5_2,
  output A14,
  output D_CPU_6_2,
  output D_CPU_7_2
);

  wire and_1_out, and_2_out;

  assign {D7_2, D6_2, D5_2, D4_2, D3_2, D2_2, D1_2, D0_2} = and_1_out ? {D_CPU_7, D_CPU_6, D_CPU_5, D_CPU_4, D_CPU_3, D_CPU_2, D_CPU_1, D_CPU_0} : 8'bz;  // Controlled_Buffer controlled_buffer_1
  and and_1 (and_1_out, ~R_W, ENA);  // AND_Gate
  and and_2 (and_2_out, R_W, ENA);
  assign {D_CPU_7_2, D_CPU_6_2, D_CPU_5_2, D_CPU_4_2, D_CPU_3_2, D_CPU_2_2, D_CPU_1_2, D_CPU_0_2} = and_2_out ? {D7, D6, D5, D4, D3, D2, D1, D0} : 8'bz;  // Controlled_Buffer controlled_buffer_2

  assign A0 = A_CPU_0;
  assign A1 = A_CPU_1;
  assign A2 = A_CPU_2;
  assign A3 = A_CPU_3;
  assign A4 = A_CPU_4;
  assign A5 = A_CPU_5;
  assign A6 = A_CPU_6;
  assign A7 = A_CPU_7;
  assign A8 = A_CPU_8;
  assign A9 = A_CPU_9;
  assign A10 = A_CPU_10;
  assign A11 = A_CPU_11;
  assign A12 = A_CPU_12;
  assign A13 = A_CPU_13;
  assign A14 = A_CPU_14;
  assign CLK_2 = CLK;
  assign ENA_2 = ENA;
  assign GND_2 = GND;
  assign PWR_2 = PWR;
  assign R_W_2 = R_W;
  assign RST_2 = RST;
endmodule

module seq_coder (
  input  [7:0] D,
  input  CLK,
  input  L,
  output out_4
);

  wire d_ff_1_q, d_ff_2_q, d_ff_3_q, d_ff_4_q, d_ff_5_q, d_ff_6_q, d_ff_7_q, d_ff_8_q, multiplexer_1_out,
       multiplexer_2_out, multiplexer_3_out, multiplexer_4_out, multiplexer_5_out, multiplexer_6_out,
       multiplexer_7_out, multiplexer_8_out, multiplexer_9_out;

  D_Flip_Flop d_ff_1 (.clk(CLK), .D(multiplexer_1_out), .Q(d_ff_1_q));  // open: Qn, preset, reset
  Multiplexer #(.enable("false")) multiplexer_1 (.in0(1'b0), .in1(D[0]), .out(multiplexer_1_out), .sel(L));
  D_Flip_Flop d_ff_2 (.clk(CLK), .D(multiplexer_2_out), .Q(d_ff_2_q));  // open: Qn, preset, reset
  Multiplexer #(.enable("false")) multiplexer_2 (.in0(d_ff_1_q), .in1(D[1]), .out(multiplexer_2_out), .sel(L));
  Multiplexer #(.enable("false")) multiplexer_3 (.in0(d_ff_2_q), .in1(D[2]), .out(multiplexer_3_out), .sel(L));
  D_Flip_Flop d_ff_3 (.clk(CLK), .D(multiplexer_3_out), .Q(d_ff_3_q));  // open: Qn, preset, reset
  Multiplexer #(.enable("false")) multiplexer_4 (.in0(d_ff_3_q), .in1(D[3]), .out(multiplexer_4_out), .sel(L));
  D_Flip_Flop d_ff_4 (.clk(CLK), .D(multiplexer_4_out), .Q(d_ff_4_q));  // open: Qn, preset, reset
  D_Flip_Flop d_ff_5 (.clk(CLK), .D(multiplexer_5_out), .Q(d_ff_5_q));  // open: Qn, preset, reset
  Multiplexer #(.enable("false")) multiplexer_5 (.in0(d_ff_4_q), .in1(D[4]), .out(multiplexer_5_out), .sel(L));
  D_Flip_Flop d_ff_6 (.clk(CLK), .D(multiplexer_6_out), .Q(d_ff_6_q));  // open: Qn, preset, reset
  Multiplexer #(.enable("false")) multiplexer_6 (.in0(d_ff_5_q), .in1(D[5]), .out(multiplexer_6_out), .sel(L));
  Multiplexer #(.enable("false")) multiplexer_7 (.in0(d_ff_6_q), .in1(D[6]), .out(multiplexer_7_out), .sel(L));
  D_Flip_Flop d_ff_7 (.clk(CLK), .D(multiplexer_7_out), .Q(d_ff_7_q));  // open: Qn, preset, reset
  Multiplexer #(.enable("false")) multiplexer_8 (.in0(d_ff_7_q), .in1(D[7]), .out(multiplexer_8_out), .sel(L));
  D_Flip_Flop d_ff_8 (.clk(CLK), .D(multiplexer_8_out), .Q(d_ff_8_q));  // open: Qn, preset, reset
  D_Flip_Flop d_ff_9 (.clk(CLK), .D(multiplexer_9_out), .Q(out_4));  // open: Qn, preset, reset
  Multiplexer #(.enable("false")) multiplexer_9 (.in0(d_ff_8_q), .in1(L), .out(multiplexer_9_out), .sel(L));
endmodule
