// Logisim project keyboard_logic.circ as structural Verilog: 1 circuit, main circuit main
module main (
  input  [6:0] in_1,
  input  ALT,
  input  CTRL,
  input  SFT,
  input  ENTER,
  input  ESC,
  input  UP,
  input  DOWN,
  input  RIGHT,
  input  LEFT,
  input  DEL,
  input  BS,
  input  TAB,
  output [7:0] out_14
);

  wire and_1_out, and_2_out, and_3_out, and_4_out, and_6_out, and_7_out, and_8_out, and_10_out, and_11_out,
       and_12_out, and_13_out, and_14_out, and_15_out, and_16_out, nor_1_out, not_1_out, not_2_out, or_1_out,
       or_2_out, or_3_out, or_4_out, or_5_out, or_6_out, or_7_out, or_8_out, or_9_out, or_12_out, or_13_out,
       or_14_out, or_15_out, or_19_out, or_20_out, or_21_out, or_22_out, or_23_out, or_24_out;
  wire [6:0] or_16_out;
  wire [7:0] controlled_buffer_1_out;

  // Probe on in_1
  // Probe on in_1
  not not_1 (not_1_out, CTRL);
  or or_1 (or_1_out, ENTER, ESC);
  or or_2 (or_2_out, UP, DOWN);
  or or_3 (or_3_out, RIGHT, LEFT);
  or or_4 (or_4_out, DEL, BS);
  and and_1 (and_1_out, in_1[5], in_1[4]);
  or or_5 (or_5_out, in_1[3], in_1[2]);
  or or_6 (or_6_out, in_1[1], in_1[0]);
  or or_7 (or_7_out, in_1[5], SFT);
  and and_2 (and_2_out, SFT, and_3_out);
  and and_3 (and_3_out, in_1[5], in_1[4]);
  or or_8 (or_8_out, or_1_out, or_2_out);
  or or_9 (or_9_out, or_3_out, or_4_out);
  nor nor_1 (nor_1_out, or_5_out, or_6_out);
  and and_4 (and_4_out, nor_1_out, and_1_out);
  or or_10 (or_16_out[2], and_8_out, in_1[2]);
  or or_11 (or_16_out[3], and_8_out, in_1[3]);
  or or_12 (or_12_out, and_8_out, in_1[6]);
  and and_5 (or_16_out[5], ~and_8_out, or_7_out);  // AND_Gate
  and and_6 (and_6_out, in_1[4], ~and_2_out);  // AND_Gate
  or or_13 (or_13_out, or_8_out, or_9_out);
  or or_14 (or_14_out, or_13_out, TAB);
  assign controlled_buffer_1_out = ENTER ? 8'hd : 8'bz;  // Controlled_Buffer controlled_buffer_1
  assign controlled_buffer_1_out = and_7_out ? 8'h1b : 8'bz;  // Controlled_Buffer controlled_buffer_2
  and and_7 (and_7_out, ~ENTER, ESC);  // AND_Gate
  or or_15 (or_15_out, ENTER, ESC);
  and and_8 (and_8_out, and_4_out, ~and_6_out);  // AND_Gate
  or or_16 (or_16_out[0], and_8_out, in_1[0]);
  or or_17 (or_16_out[1], and_8_out, in_1[1]);
  or or_18 (or_16_out[4], and_6_out, and_8_out);
  and and_9 (or_16_out[6], or_12_out, not_1_out);
  assign controlled_buffer_1_out = and_10_out ? 8'h1 : 8'bz;  // Controlled_Buffer controlled_buffer_3
  and and_10 (and_10_out, ~or_15_out, UP);  // AND_Gate
  or or_19 (or_19_out, or_15_out, UP);
  assign out_14 = not_2_out ? {ALT, or_16_out} : 8'bz;  // Controlled_Buffer controlled_buffer_4
  not not_2 (not_2_out, or_14_out);
  assign controlled_buffer_1_out = and_11_out ? 8'h2 : 8'bz;  // Controlled_Buffer controlled_buffer_5
  and and_11 (and_11_out, ~or_19_out, DOWN);  // AND_Gate
  or or_20 (or_20_out, or_19_out, DOWN);
  // Probe on out_14
  // Probe on out_14
  assign out_14 = or_14_out ? controlled_buffer_1_out : 8'bz;  // Controlled_Buffer controlled_buffer_6
  assign controlled_buffer_1_out = and_12_out ? 8'h3 : 8'bz;  // Controlled_Buffer controlled_buffer_7
  and and_12 (and_12_out, ~or_20_out, RIGHT);  // AND_Gate
  or or_21 (or_21_out, or_20_out, RIGHT);
  assign controlled_buffer_1_out = and_13_out ? 8'h4 : 8'bz;  // Controlled_Buffer controlled_buffer_8
  and and_13 (and_13_out, ~or_21_out, LEFT);  // AND_Gate
  or or_22 (or_22_out, or_21_out, LEFT);
  assign controlled_buffer_1_out = and_14_out ? 8'h7f : 8'bz;  // Controlled_Buffer controlled_buffer_9
  and and_14 (and_14_out, ~or_22_out, DEL);  // AND_Gate
  or or_23 (or_23_out, or_22_out, DEL);
  assign controlled_buffer_1_out = and_15_out ? 8'h8 : 8'bz;  // Controlled_Buffer controlled_buffer_10
  and and_15 (and_15_out, ~or_23_out, BS);  // AND_Gate
  or or_24 (or_24_out, or_23_out, BS);
  assign controlled_buffer_1_out = and_16_out ? 8'h9 : 8'bz;  // Controlled_Buffer controlled_buffer_11
  and and_16 (and_16_out, ~or_24_out, TAB);  // AND_Gate
endmodule
