// Logisim project random.circ as structural Verilog: 1 circuit, main circuit main
module main (
  input  in_1,
  output [7:0] out_2
);

  wire and_1_out, clock_1_out, counter_1_carry, d_ff_1_q, xor_1_out;
  wire [8:0] counter_1_q;

  and and_1 (and_1_out, clock_1_out, ~counter_1_carry);  // AND_Gate
  Clock clock_1 (.out(clock_1_out));
  D_Flip_Flop d_ff_1 (.clk(and_1_out), .D(xor_1_out), .Q(d_ff_1_q), .preset(in_1));  // open: Qn, reset
  D_Flip_Flop d_ff_2 (.clk(and_1_out), .D(d_ff_1_q), .Q(out_2[7]), .reset(in_1));  // open: Qn, preset
  RAM #(.addrWidth(9)) ram_1 (.addr(counter_1_q), .we(and_1_out), .clk(and_1_out), .din(out_2));  // open: dout
  Counter #(.max('h1ff), .width(9)) counter_1 (
    .Q(counter_1_q), .carry(counter_1_carry), .clk(and_1_out), .clr(in_1));  // open: load, D, count
  D_Flip_Flop d_ff_3 (.clk(and_1_out), .D(out_2[7]), .Q(out_2[6]), .reset(in_1));  // open: Qn, preset
  D_Flip_Flop d_ff_4 (.clk(and_1_out), .D(out_2[6]), .Q(out_2[5]), .reset(in_1));  // open: Qn, preset
  xor xor_1 (xor_1_out, out_2[5], out_2[0]);
  D_Flip_Flop d_ff_5 (.clk(and_1_out), .D(out_2[5]), .Q(out_2[4]), .reset(in_1));  // open: Qn, preset
  D_Flip_Flop d_ff_6 (.clk(and_1_out), .D(out_2[4]), .Q(out_2[3]), .reset(in_1));  // open: Qn, preset
  D_Flip_Flop d_ff_7 (.clk(and_1_out), .D(out_2[3]), .Q(out_2[2]), .reset(in_1));  // open: Qn, preset
  D_Flip_Flop d_ff_8 (.clk(and_1_out), .D(out_2[2]), .Q(out_2[1]), .reset(in_1));  // open: Qn, preset
  D_Flip_Flop d_ff_9 (.clk(and_1_out), .D(out_2[1]), .Q(out_2[0]), .reset(in_1));  // open: Qn, preset
endmodule
